// Logisim project circuito_mux_7segs.circ as structural Verilog
module main (
  input  [3:0] ABCD,
  input  [3:0] ABCD_HDL
);

  wire [6:0] dec_7s_muxes_1_abcdefg, mux_1_hex0;

  _7_Segment_Display u_7_segment_display_1 (
    .g(mux_1_hex0[0]), .f(mux_1_hex0[1]), .a(mux_1_hex0[6]), .b(mux_1_hex0[5]), .e(mux_1_hex0[2]),
    .d(mux_1_hex0[3]), .c(mux_1_hex0[4]));  // open: dp
  _7_Segment_Display u_7_segment_display_2 (
    .g(dec_7s_muxes_1_abcdefg[0]), .f(dec_7s_muxes_1_abcdefg[1]), .a(dec_7s_muxes_1_abcdefg[6]),
    .b(dec_7s_muxes_1_abcdefg[5]), .e(dec_7s_muxes_1_abcdefg[2]), .d(dec_7s_muxes_1_abcdefg[3]),
    .c(dec_7s_muxes_1_abcdefg[4]));  // open: dp
  dec_7s_muxes dec_7s_muxes_1 (.ABCD(ABCD), .abcdefg(dec_7s_muxes_1_abcdefg));
  mux mux_1 (.SW(ABCD_HDL), .HEX0(mux_1_hex0));
endmodule

module dec_7s_muxes (
  input  [3:0] ABCD,
  output [6:0] abcdefg
);

  Multiplexer #(.select(4)) multiplexer_1 (
    .in0(1'b1), .in1(1'b0), .in2(1'b1), .in3(1'b1), .in4(1'b0), .in5(1'b1), .in6(1'b1), .in7(1'b1),
    .in8(1'b1), .in9(1'b1), .in10(1'b1), .in11(1'b0), .in12(1'b1), .in13(1'b0), .in14(1'b1), .in15(1'b0),
    .out(abcdefg[6]), .sel(ABCD));
  Multiplexer #(.select(4)) multiplexer_2 (
    .in0(1'b1), .in1(1'b1), .in2(1'b1), .in3(1'b1), .in4(1'b1), .in5(1'b0), .in6(1'b0), .in7(1'b1),
    .in8(1'b1), .in9(1'b1), .in10(1'b1), .in11(1'b0), .in12(1'b0), .in13(1'b1), .in14(1'b1), .in15(1'b1),
    .out(abcdefg[5]), .sel(ABCD));
  Multiplexer #(.select(4)) multiplexer_3 (
    .in0(1'b1), .in1(1'b1), .in2(1'b0), .in3(1'b1), .in4(1'b1), .in5(1'b1), .in6(1'b1), .in7(1'b1),
    .in8(1'b1), .in9(1'b1), .in10(1'b1), .in11(1'b1), .in12(1'b0), .in13(1'b1), .in14(1'b1), .in15(1'b1),
    .out(abcdefg[4]), .sel(ABCD));
  Multiplexer #(.select(4)) multiplexer_4 (
    .in0(1'b1), .in1(1'b0), .in2(1'b1), .in3(1'b1), .in4(1'b0), .in5(1'b1), .in6(1'b1), .in7(1'b0),
    .in8(1'b1), .in9(1'b1), .in10(1'b0), .in11(1'b1), .in12(1'b1), .in13(1'b1), .in14(1'b1), .in15(1'b1),
    .out(abcdefg[3]), .sel(ABCD));
  Multiplexer #(.select(4)) multiplexer_5 (
    .in0(1'b1), .in1(1'b0), .in2(1'b1), .in3(1'b0), .in4(1'b0), .in5(1'b0), .in6(1'b1), .in7(1'b0),
    .in8(1'b1), .in9(1'b0), .in10(1'b1), .in11(1'b1), .in12(1'b1), .in13(1'b1), .in14(1'b0), .in15(1'b1),
    .out(abcdefg[2]), .sel(ABCD));
  Multiplexer #(.select(4)) multiplexer_6 (
    .in0(1'b1), .in1(1'b0), .in2(1'b0), .in3(1'b0), .in4(1'b1), .in5(1'b1), .in6(1'b1), .in7(1'b0),
    .in8(1'b1), .in9(1'b1), .in10(1'b1), .in11(1'b1), .in12(1'b1), .in13(1'b0), .in14(1'b1), .in15(1'b0),
    .out(abcdefg[1]), .sel(ABCD));
  Multiplexer #(.select(4)) multiplexer_7 (
    .in0(1'b0), .in1(1'b0), .in2(1'b1), .in3(1'b1), .in4(1'b1), .in5(1'b1), .in6(1'b1), .in7(1'b0),
    .in8(1'b1), .in9(1'b1), .in10(1'b1), .in11(1'b1), .in12(1'b0), .in13(1'b1), .in14(1'b1), .in15(1'b0),
    .out(abcdefg[0]), .sel(ABCD));

  // Other names for the same wires on the sheet: A = ABCD[0]; B = ABCD[1]; C = ABCD[2]; D = ABCD[3]; g = abcdefg[0];
  //   f = abcdefg[1]; e = abcdefg[2]; d_t = abcdefg[3]; c_t = abcdefg[4]; b_t = abcdefg[5]; a_t = abcdefg[6]
endmodule

// VHDL entity mux, as the project stores it:
--------------------------------------------------------------------------------
-- Project :
-- File    :
-- Autor   :
-- Date    :
--
--------------------------------------------------------------------------------
-- Description :
--
--------------------------------------------------------------------------------

LIBRARY ieee;
USE ieee.std_logic_1164.all;
USE ieee.numeric_std.all;

ENTITY mux IS
  PORT (
	SW 	: in  std_logic_vector(3 downto 0); -- Chaves de A(0) até D(3)
	HEX0 : out std_logic_vector(6 downto 0) -- Segmentos de a(6) até g(0)
    );
END mux;

--------------------------------------------------------------------------------
-- MUX logic
--------------------------------------------------------------------------------

ARCHITECTURE TypeArchitecture OF mux IS

	-- Cria um tipo que é um array do qual cada elemento contém um vetor de 7 bits
	type display_rom is array (0 to 15) of std_logic_vector(6 downto 0); 

	-- Preenche a lista com a tabela verdade
	constant MAPA_7SEG : display_rom := (
	   "1111110", -- Índice 0 (Hex 0)
        "0110000", -- Índice 1 (Hex 1)
        "1101101", -- Índice 2 (Hex 2)
        "1111001", -- Índice 3 (Hex 3)
        "0110011", -- Índice 4 (Hex 4)
        "1011011", -- Índice 5 (Hex 5)
        "1011111", -- Índice 6 (Hex 6)
        "1110000", -- Índice 7 (Hex 7)
        "1111111", -- Índice 8 (Hex 8)
        "1111011", -- Índice 9 (Hex 9)
        "1110111", -- Índice 10 (Hex A)
        "0011111", -- Índice 11 (Hex B)
        "1001110", -- Índice 12 (Hex C)
        "0111101", -- Índice 13 (Hex D)
        "1111011", -- Índice 14 (Hex E -> O dígito '9')
        "0111100"  -- Índice 15 (Hex F -> A letra 'J')		
	);
	
    -- CRIA O FIO INTERMEDIÁRIO 
    signal sw_invertido : std_logic_vector(3 downto 0);

BEGIN

	sw_invertido <= not SW;

	-- Pegamos os 4 bits da chave física (SW), transformamos em número inteiro 
     -- e jogamos o resultado da tabela direto para os pinos do display (HEX0)
	HEX0 <= MAPA_7SEG(to_integer(unsigned(sw_invertido)));

END TypeArchitecture;
