// Logisim project circuito_mux_7segs_clock.circ as structural Verilog
module main (
  input  in_1,
  input  in_2,
  input  in_3,
  input  in_4
);

  wire clk_out, clock_debouncer_out;
  wire [3:0] counter_1_q;
  wire [6:0] dec_7s_muxes_1_abcdefg, mux_1_hex0, mux_counter_alone_1_hex0;

  Clock clk (.out(clk_out));
  Counter #(.max('hf), .width(4)) counter_1 (.clk(clk_out), .Q(counter_1_q));  // open: clr, load, up, count, D, carry
  _7_Segment_Display u_7_segment_display_1 (
    .g(mux_1_hex0[0]), .f(mux_1_hex0[1]), .a(mux_1_hex0[6]), .b(mux_1_hex0[5]), .e(mux_1_hex0[2]),
    .d(mux_1_hex0[3]), .c(mux_1_hex0[4]));  // open: dp
  _7_Segment_Display u_7_segment_display_2 (
    .g(dec_7s_muxes_1_abcdefg[0]), .f(dec_7s_muxes_1_abcdefg[1]), .a(dec_7s_muxes_1_abcdefg[6]),
    .b(dec_7s_muxes_1_abcdefg[5]), .e(dec_7s_muxes_1_abcdefg[2]), .d(dec_7s_muxes_1_abcdefg[3]),
    .c(dec_7s_muxes_1_abcdefg[4]));  // open: dp
  mux mux_1 (.CLK(in_3), .CLEAR(in_4), .HEX0(mux_1_hex0));
  dec_7s_muxes dec_7s_muxes_1 (.ABCD(counter_1_q), .abcdefg(dec_7s_muxes_1_abcdefg));
  Clock clock_debouncer (.out(clock_debouncer_out));
  _7_Segment_Display u_7_segment_display_3 (
    .g(mux_counter_alone_1_hex0[0]), .f(mux_counter_alone_1_hex0[1]), .a(mux_counter_alone_1_hex0[6]),
    .b(mux_counter_alone_1_hex0[5]), .e(mux_counter_alone_1_hex0[2]), .d(mux_counter_alone_1_hex0[3]),
    .c(mux_counter_alone_1_hex0[4]));  // open: dp
  mux_counter_alone mux_counter_alone_1 (
    .clock_50MHz(clock_debouncer_out), .START(in_1), .CLEAR(in_2), .HEX0(mux_counter_alone_1_hex0));
endmodule

module dec_7s_muxes (
  input  [3:0] ABCD,
  output [6:0] abcdefg
);

  Multiplexer #(.select(4)) multiplexer_1 (
    .in0(1'b1), .in1(1'b0), .in2(1'b1), .in3(1'b1), .in4(1'b0), .in5(1'b1), .in6(1'b1), .in7(1'b1),
    .in8(1'b1), .in9(1'b1), .in10(1'b1), .in11(1'b0), .in12(1'b1), .in13(1'b0), .in14(1'b1), .in15(1'b0),
    .out(abcdefg[6]), .sel(ABCD));
  Multiplexer #(.select(4)) multiplexer_2 (
    .in0(1'b1), .in1(1'b1), .in2(1'b1), .in3(1'b1), .in4(1'b1), .in5(1'b0), .in6(1'b0), .in7(1'b1),
    .in8(1'b1), .in9(1'b1), .in10(1'b1), .in11(1'b0), .in12(1'b0), .in13(1'b1), .in14(1'b1), .in15(1'b1),
    .out(abcdefg[5]), .sel(ABCD));
  Multiplexer #(.select(4)) multiplexer_3 (
    .in0(1'b1), .in1(1'b1), .in2(1'b0), .in3(1'b1), .in4(1'b1), .in5(1'b1), .in6(1'b1), .in7(1'b1),
    .in8(1'b1), .in9(1'b1), .in10(1'b1), .in11(1'b1), .in12(1'b0), .in13(1'b1), .in14(1'b1), .in15(1'b1),
    .out(abcdefg[4]), .sel(ABCD));
  Multiplexer #(.select(4)) multiplexer_4 (
    .in0(1'b1), .in1(1'b0), .in2(1'b1), .in3(1'b1), .in4(1'b0), .in5(1'b1), .in6(1'b1), .in7(1'b0),
    .in8(1'b1), .in9(1'b1), .in10(1'b0), .in11(1'b1), .in12(1'b1), .in13(1'b1), .in14(1'b1), .in15(1'b1),
    .out(abcdefg[3]), .sel(ABCD));
  Multiplexer #(.select(4)) multiplexer_5 (
    .in0(1'b1), .in1(1'b0), .in2(1'b1), .in3(1'b0), .in4(1'b0), .in5(1'b0), .in6(1'b1), .in7(1'b0),
    .in8(1'b1), .in9(1'b0), .in10(1'b1), .in11(1'b1), .in12(1'b1), .in13(1'b1), .in14(1'b0), .in15(1'b1),
    .out(abcdefg[2]), .sel(ABCD));
  Multiplexer #(.select(4)) multiplexer_6 (
    .in0(1'b1), .in1(1'b0), .in2(1'b0), .in3(1'b0), .in4(1'b1), .in5(1'b1), .in6(1'b1), .in7(1'b0),
    .in8(1'b1), .in9(1'b1), .in10(1'b1), .in11(1'b1), .in12(1'b1), .in13(1'b0), .in14(1'b1), .in15(1'b0),
    .out(abcdefg[1]), .sel(ABCD));
  Multiplexer #(.select(4)) multiplexer_7 (
    .in0(1'b0), .in1(1'b0), .in2(1'b1), .in3(1'b1), .in4(1'b1), .in5(1'b1), .in6(1'b1), .in7(1'b0),
    .in8(1'b1), .in9(1'b1), .in10(1'b1), .in11(1'b1), .in12(1'b0), .in13(1'b1), .in14(1'b1), .in15(1'b0),
    .out(abcdefg[0]), .sel(ABCD));

  // Other names for the same wires on the sheet: A = ABCD[0]; B = ABCD[1]; C = ABCD[2]; D = ABCD[3]; g = abcdefg[0];
  //   f = abcdefg[1]; e = abcdefg[2]; d_t = abcdefg[3]; c_t = abcdefg[4]; b_t = abcdefg[5]; a_t = abcdefg[6]
endmodule

// VHDL entity mux, as the project stores it:
LIBRARY ieee;
USE ieee.std_logic_1164.all;
USE ieee.numeric_std.all;

ENTITY mux IS
  PORT (
    CLK   : in  std_logic; -- 1 bit (Fio único do botão)
    CLEAR : in  std_logic; -- 1 bit (Fio único do botão)
    HEX0  : out std_logic_vector(6 downto 0) -- 7 bits (Segmentos)
  ); 
END mux;

--------------------------------------------------------------------------------
-- MUX logic
--------------------------------------------------------------------------------

ARCHITECTURE TypeArchitecture OF mux IS

    -- Array da ROM (Display)
    type display_rom is array (0 to 15) of std_logic_vector(6 downto 0); 

    constant MAPA_7SEG : display_rom := (
        "1111110", -- 0
        "0110000", -- 1
        "1101101", -- 2
        "1111001", -- 3
        "0110011", -- 4
        "1011011", -- 5
        "1011111", -- 6
        "1110000", -- 7
        "1111111", -- 8
        "1111011", -- 9
        "1110111", -- A
        "0011111", -- B
        "1001110", -- C
        "0111101", -- D
        "1111011", -- E (Dígito 9)
        "0111100"  -- F (Letra J)        
    );
    
    -- Sinais internos invertidos
    signal clock_inv : std_logic;
    signal clear_inv : std_logic;

    -- Guarda a contagem atual
    signal count : unsigned(3 downto 0) := "0000";
    
BEGIN

    -- Inversão da lógica active-low dos botões físicos
    clock_inv <= not CLK;
    clear_inv <= not CLEAR;

    -- O ideal é que a lista de sensibilidade monitore os sinais que ela realmente testa
    process(clock_inv, clear_inv)
    begin 
        -- Zera assincronamente se o botão Clear for apertado
        if clear_inv = '1' then
            count <= "0000";
    
        -- Senão, detecta a batida do relógio (Quando APERTA o botão físico)
        elsif rising_edge(clock_inv) then
            count <= count + 1;
        end if;
    end process;
        
    -- Converte a contagem para integer para poder achar a "gaveta" correta da ROM
    HEX0 <= MAPA_7SEG(to_integer(count));

END TypeArchitecture;

// VHDL entity mux_debounce, as the project stores it:
LIBRARY ieee;
USE ieee.std_logic_1164.all;
USE ieee.numeric_std.all;

ENTITY mux_debounce IS
  PORT (
    clock_50MHz : in  std_logic; -- Clock da placa
    CLK_BTN     : in  std_logic; -- 1 bit (Fio único do botão)
    CLEAR       : in  std_logic; -- 1 bit (Fio único do botão)
    HEX0  	 : out std_logic_vector(6 downto 0) -- 7 bits (Segmentos)
  );
END mux_debounce;

--------------------------------------------------------------------------------
-- MUX logic
--------------------------------------------------------------------------------

ARCHITECTURE RTL OF mux_debounce IS

    -- Array da ROM (Display)
    type display_rom is array (0 to 15) of std_logic_vector(6 downto 0); 

    constant MAPA_7SEG : display_rom := (
        "1111110", -- 0
        "0110000", -- 1
        "1101101", -- 2
        "1111001", -- 3
        "0110011", -- 4
        "1011011", -- 5
        "1011111", -- 6
        "1110000", -- 7
        "1111111", -- 8
        "1111011", -- 9
        "1110111", -- A
        "0011111", -- B
        "1001110", -- C
        "0111101", -- D
        "1111011", -- E (Dígito 9)
        "0111100"  -- F (Letra J)        
    );
    
    -- Fios internos 
    signal clock_btn_inv : std_logic; -- Botão de clock invertido
    signal clear_btn_inv : std_logic; -- Botão de clear invertido
    signal pulse_cleared : std_logic; -- Pulso limpo
    signal count : unsigned(3 downto 0) := "0000";

    -- Declarando componente de Deobouncer
	COMPONENT debouncer IS
        PORT ( CLOCK, BTN_IN : in std_logic; BTN_OUT : out std_logic );
     END COMPONENT;
    
BEGIN

    -- Inversão da lógica active-low dos botões físicos
    clear_btn_inv  <= not CLEAR;

    -- Conectando a caixinha: Entra o botão sujo, sai o botão limpo.
    -- O 'clk_50MHz' faz a matemática do tempo.
    U1: debouncer PORT MAP (
        CLOCK   => clock_50MHz,
        BTN_IN  => CLK_BTN,
        BTN_OUT => pulse_cleared
    );

    clock_btn_inv <= not pulse_cleared;
    

    -- O ideal é que a lista de sensibilidade monitore os sinais que ela realmente testa
    process(clock_btn_inv, clear_btn_inv)
    begin 
        -- Zera assincronamente se o botão Clear for apertado
        if clear_btn_inv = '1' then
            count <= "0000";
    
        -- Senão, detecta a batida do relógio (Quando APERTA o botão físico)
        elsif rising_edge(clock_btn_inv) then
            count <= count + 1;
        end if;
    end process;
        
    -- Converte a contagem para integer para poder achar a "gaveta" correta da ROM
    HEX0 <= MAPA_7SEG(to_integer(count));

END RTL;

// VHDL entity debouncer, as the project stores it:
LIBRARY ieee;
USE ieee.std_logic_1164.all;
USE ieee.numeric_std.all;

ENTITY debouncer IS
  GENERIC (
        -- Tempo necessário para confirmar a estabilidade.
        -- Para 50MHz, 1.000.000 de ciclos = 20 milissegundos.
        TEMPO_MAX : integer := 1000000
  );
  
  PORT (
	CLOCK   : in std_logic; -- Clock de 50MHz da placa
	BTN_IN  : in std_logic; -- Sinal "sujo" 
	BTN_OUT : out std_logic -- Sinal "limpo"
    );
END debouncer;

--------------------------------------------------------------------------------
-- DEBOUNCER LOGIC
--------------------------------------------------------------------------------

ARCHITECTURE RTL OF debouncer IS
	-- Contador que conta de 0 até o tempo máximo estipulado em clocks
	signal counter : integer range 0 to TEMPO_MAX := 0;
	-- Guarda qual é o estado limpo atual (0 ou 1)
	signal clean_state : std_logic :=  '0';

BEGIN

	process(CLOCK)
	-- Se o botão físico estiver diferente do estado que consideramos "limpo"
	begin
		if rising_edge(CLOCK) then
			if BTN_IN /= clean_state then
				counter <= counter + 1;
	
				if counter = TEMPO_MAX then
					clean_state <= BTN_IN;
					counter <= 0;
				end if;
			else 
				-- Se ele trepidar no meio da contagem, ou se já forem iguais, zera o timer
	                counter <= 0;
	                
	          end if;
	     end if;
     end process;

     BTN_OUT <= clean_state;
			
END RTL;

// VHDL entity mux_counter_alone, as the project stores it:
LIBRARY ieee;
USE ieee.std_logic_1164.all;
USE ieee.numeric_std.all;

ENTITY mux_counter_alone IS
  GENERIC (
        -- Tempo necessário para confirmar a estabilidade.
        -- Para 50MHz, 50.000.000 de ciclos = 1000 milissegundos ou 1 segundo.
        TEMPO_1S : integer := 50000000
  );

  PORT (
    clock_50MHz : in  std_logic; -- Clock da placa
    START       : in  std_logic; -- 1 bit (Fio único do botão)
    CLEAR       : in  std_logic; -- 1 bit (Fio único do botão)
    HEX0  	 : out std_logic_vector(6 downto 0) -- 7 bits (Segmentos)
  );
END mux_counter_alone;

--------------------------------------------------------------------------------
-- MUX logic
--------------------------------------------------------------------------------

ARCHITECTURE RTL OF mux_counter_alone IS

    -- Array da ROM (Display)
    type display_rom is array (0 to 15) of std_logic_vector(6 downto 0); 

    constant MAPA_7SEG : display_rom := (
        "1111110", -- 0
        "0110000", -- 1
        "1101101", -- 2
        "1111001", -- 3
        "0110011", -- 4
        "1011011", -- 5
        "1011111", -- 6
        "1110000", -- 7
        "1111111", -- 8
        "1111011", -- 9
        "1110111", -- A
        "0011111", -- B
        "1001110", -- C
        "0111101", -- D
        "1111011", -- E (Dígito 9)
        "0111100"  -- F (Letra J)        
    );
    
    -- Fios internos 
    signal start_inv     : std_logic; -- Botão de clock invertido
    signal clear_inv     : std_logic; -- Botão de clear invertido
    signal pulse_cleared : std_logic; -- Pulso limpo
    signal count         : unsigned(3 downto 0) := "0000";
    -- Contador que conta de 0 até o tempo de um segundo segundo o clock 
    signal counter       : integer range 0 to TEMPO_1S := 0;
    -- Memória do botão
    signal pause         : std_logic := '0'; -- 0 = rodando, 1 = pausado
    signal previous_state: std_logic := '1'; -- Memória para detectar clique

    -- Declarando componente de Deobouncer
	COMPONENT debouncer IS
        PORT ( CLOCK, BTN_IN : in std_logic; BTN_OUT : out std_logic );
     END COMPONENT;
    
BEGIN

    -- Inversão da lógica active-low dos botões físicos
    clear_inv  <= not CLEAR;

    -- Conectando a caixinha: Entra o botão sujo, sai o botão limpo.
    -- O 'clk_50MHz' faz a matemática do tempo.
    U1: debouncer PORT MAP (
        CLOCK   => clock_50MHz,
        BTN_IN  => START,
        BTN_OUT => pulse_cleared
    );

    start_inv <= not pulse_cleared;
    
    process(clock_50MHz, clear_inv)
    begin 
	   -- Rset
	   if clear_inv = '1' then
	       count <= "0000";
 		  counter <= 0;
 		  pause <= '0';
 		  previous_state <= '1';

	   -- Motor do clock
	   elsif rising_edge(clock_50MHz) then

		 -- ====================================================
           -- BLOCO A: Detecção do Botão (Toggle Play/Pause)
           -- ====================================================
		if previous_state = '0' and start_inv = '1' then
			pause <= not pause;
          end if;
		previous_state <= start_inv;


		 -- ====================================================
           -- BLOCO B: O Cronômetro (O Clock Enable)
           -- ====================================================
           if pause = '0' then
		 	 if counter = TEMPO_1S -1 then
	      		count <= count + 1;
	      		counter <= 0;
	      	else
	      		counter <= counter + 1;
	      	end if;
	      end if;
	   end if;
    end process;
        
    -- Converte a contagem para integer para poder achar a "gaveta" correta da ROM
    HEX0 <= MAPA_7SEG(to_integer(count));

END RTL;
